// Logisim project TP_7.circ as structural Verilog: 2 circuits, main circuit main
module main (
);

  wire alu_1_zero, ALUSrc, and_1_out, and_2_out, and_3_out, and_4_out, and_5_out, Branch, CLK,
       decoder_1_out0, decoder_1_out1, decoder_1_out2, decoder_1_out3, MemRead, MemToReg, MemWrite, RegDst,
       RegWrite, Reiniciar, ReiniciarManual;
  wire [0:0] Unidad_De_Control_data;
  wire [1:0] multiplexer_1_out;
  wire [2:0] ALUOP;
  wire [7:0] A, adder_1_out, adder_2_out, alu_1_salida, B, C, D_q, Memoria_dout, multiplexer_2_out,
       multiplexer_3_out, multiplexer_4_out, multiplexer_5_out, multiplexer_6_out, PC_q;
  wire [15:0] rom_1_data;

  _7_Segment_Display u_7_segment_display_1 ();  // open: g, f, a, b, e, d, c, dp
  // BCD_to_7_Segment_decoder bcd_to_7_segment_decoder_1: pin names not known
  _7_Segment_Display u_7_segment_display_2 ();  // open: g, f, a, b, e, d, c, dp
  // BCD_to_7_Segment_decoder bcd_to_7_segment_decoder_2: pin names not known
  // Binary_to_BCD_converter #(.binvalue(8)) binary_to_bcd_converter_1: pin names not known; wires that end beside it: A
  Register PC (.D(multiplexer_5_out), .en(CLK), .clk(CLK), .Q(PC_q), .clr(Reiniciar));
  _7_Segment_Display u_7_segment_display_3 ();  // open: g, f, a, b, e, d, c, dp
  // BCD_to_7_Segment_decoder bcd_to_7_segment_decoder_3: pin names not known
  ROM #(.dataWidth(16)) rom_1 (.addr(PC_q), .data(rom_1_data));
  Button button_1 (.out(ReiniciarManual));
  Clock clock_1 (.out(CLK));
  Adder adder_1 (.a(8'h1), .b(PC_q), .out(adder_1_out));  // open: cin, cout
  _7_Segment_Display u_7_segment_display_4 ();  // open: g, f, a, b, e, d, c, dp
  // BCD_to_7_Segment_decoder bcd_to_7_segment_decoder_4: pin names not known
  // Binary_to_BCD_converter #(.binvalue(8)) binary_to_bcd_converter_2: pin names not known; wires that end beside it: B
  _7_Segment_Display u_7_segment_display_5 ();  // open: g, f, a, b, e, d, c, dp
  _7_Segment_Display u_7_segment_display_6 ();  // open: g, f, a, b, e, d, c, dp
  // BCD_to_7_Segment_decoder bcd_to_7_segment_decoder_5: pin names not known
  // BCD_to_7_Segment_decoder bcd_to_7_segment_decoder_6: pin names not known
  Decoder #(.enable("false"), .select(2)) decoder_1 (
    .out0(decoder_1_out0), .out1(decoder_1_out1), .out2(decoder_1_out2), .out3(decoder_1_out3),
    .sel(multiplexer_1_out));
  Multiplexer #(.width(2)) multiplexer_1 (
    .in0(rom_1_data[9:8]), .in1(rom_1_data[7:6]), .out(multiplexer_1_out), .sel(RegDst));
  _7_Segment_Display u_7_segment_display_7 ();  // open: g, f, a, b, e, d, c, dp
  // BCD_to_7_Segment_decoder bcd_to_7_segment_decoder_7: pin names not known
  // Binary_to_BCD_converter #(.binvalue(8)) binary_to_bcd_converter_3: pin names not known; wires that end beside it: C
  ROM #(.addrWidth(4), .dataWidth(11)) Unidad_De_Control (
    .addr(rom_1_data[15:12]),
    .data({ALUOP, Branch, ALUSrc, RegDst, RegWrite, MemToReg, MemWrite, MemRead, Unidad_De_Control_data[0]}));
  _7_Segment_Display u_7_segment_display_8 ();  // open: g, f, a, b, e, d, c, dp
  // BCD_to_7_Segment_decoder bcd_to_7_segment_decoder_8: pin names not known
  _7_Segment_Display u_7_segment_display_9 ();  // open: g, f, a, b, e, d, c, dp
  // BCD_to_7_Segment_decoder bcd_to_7_segment_decoder_9: pin names not known
  and and_1 (and_1_out, decoder_1_out0, RegWrite);
  and and_2 (and_2_out, decoder_1_out1, RegWrite);
  and and_3 (and_3_out, decoder_1_out2, RegWrite);
  and and_4 (and_4_out, decoder_1_out3, RegWrite);
  Register u_A (.D(multiplexer_6_out), .en(and_1_out), .clk(CLK), .Q(A), .clr(Reiniciar));
  Register u_B (.D(multiplexer_6_out), .en(and_2_out), .clk(CLK), .Q(B), .clr(Reiniciar));
  Register u_C (.D(multiplexer_6_out), .en(and_3_out), .clk(CLK), .Q(C), .clr(Reiniciar));
  Register D (.D(multiplexer_6_out), .en(and_4_out), .clk(CLK), .Q(D_q), .clr(Reiniciar));
  or or_1 (Reiniciar, Unidad_De_Control_data[0], ReiniciarManual);
  Multiplexer #(.select(2), .width(8)) multiplexer_2 (
    .in0(A), .in1(B), .in2(C), .in3(D_q), .out(multiplexer_2_out), .sel(rom_1_data[11:10]));
  Multiplexer #(.select(2), .width(8)) multiplexer_3 (
    .in0(A), .in1(B), .in2(C), .in3(D_q), .out(multiplexer_3_out), .sel(rom_1_data[9:8]));
  Multiplexer #(.width(8)) multiplexer_4 (
    .in0(multiplexer_3_out), .in1(rom_1_data[7:0]), .out(multiplexer_4_out), .sel(ALUSrc));
  Adder adder_2 (.a(adder_1_out), .b(rom_1_data[7:0]), .out(adder_2_out));  // open: cin, cout
  ALU alu_1 (
    .A(multiplexer_2_out), .Selector(ALUOP), .B(multiplexer_4_out), .Zero(alu_1_zero), .Salida(alu_1_salida));  // open: Cout
  RAM Memoria (
    .addr(alu_1_salida), .we(MemWrite), .oe(MemRead), .clk(CLK), .din(multiplexer_4_out), .dout(Memoria_dout));
  Multiplexer #(.width(8)) multiplexer_5 (
    .in0(adder_1_out), .in1(adder_2_out), .out(multiplexer_5_out), .sel(and_5_out));
  and and_5 (and_5_out, alu_1_zero, Branch);
  Multiplexer #(.width(8)) multiplexer_6 (
    .in0(alu_1_salida), .in1(Memoria_dout), .out(multiplexer_6_out), .sel(MemToReg));

  // Notes on the sheet:
  //   contents of rom_1 (hex, n*v repeats v):
  //   3000 3501 3a00 3fe9 ab04 8180 3400 3900 a0fb f000
  //   contents of Unidad_De_Control (hex, n*v repeats v):
  //   0 55a 544 550 130 230 330 430 530 630 680 4*0 1
endmodule

module ALU (
  input  [7:0] A,
  input  [2:0] Selector,
  input  [7:0] B,
  output Zero,
  output [7:0] Salida,
  output Cout
);

  wire AND0, AND1, AND2, AND3, AND4, AND5, AND6, AND7, and_2_out, and_3_out, and_4_out, and_5_out, and_6_out,
       and_7_out, and_8_out, and_9_out, and_10_out, and_11_out, and_12_out, and_13_out, and_14_out,
       and_15_out, and_16_out, and_17_out, and_18_out, and_19_out, and_20_out, and_21_out, and_22_out,
       and_23_out, and_24_out, and_25_out, and_26_out, and_27_out, and_28_out, and_29_out, and_30_out,
       and_31_out, and_32_out, and_33_out, and_34_out, and_35_out, and_36_out, and_37_out, and_38_out,
       and_39_out, and_40_out, and_41_out, and_42_out, and_43_out, and_44_out, and_45_out, and_46_out,
       and_47_out, and_48_out, and_49_out, and_50_out, and_51_out, and_52_out, and_53_out, and_54_out,
       and_55_out, and_56_out, and_57_out, and_58_out, and_59_out, and_60_out, and_61_out, and_62_out,
       and_63_out, and_64_out, and_65_out, and_66_out, and_67_out, and_68_out, and_69_out, and_70_out,
       and_71_out, and_72_out, and_73_out, and_74_out, and_75_out, and_76_out, and_77_out, and_78_out,
       and_79_out, and_80_out, and_81_out, and_82_out, and_83_out, CoutResta, CoutSuma, not_1_out, not_2_out,
       not_3_out, not_4_out, not_5_out, not_6_out, not_7_out, not_8_out, or_2_out, or_3_out, or_4_out,
       or_5_out, or_6_out, or_7_out, or_8_out, or_10_out, or_11_out, or_12_out, or_13_out, or_14_out,
       or_15_out, or_16_out, or_17_out, RES0, RES1, RES2, RES3, RES4, RES5, RES6, RES7, SUM0, SUM1, SUM2,
       SUM3, SUM4, SUM5, SUM6, SUM7, xor_1_out, xor_2_out, xor_3_out, xor_4_out, xor_5_out, xor_6_out,
       xor_7_out, xor_8_out, xor_17_out, xor_18_out, xor_19_out, xor_20_out, xor_21_out, xor_22_out,
       xor_23_out, xor_24_out;
  wire [7:0] CompNAND, CompOR, CompXOR;

  assign {AND7, AND6, AND5, AND4, AND3, AND2, AND1, AND0} = A & B;  // AND_Gate and_1, 8 bits wide
  xor xor_1 (xor_1_out, A[0], B[0]);
  xor xor_2 (xor_2_out, A[1], B[1]);
  xor xor_3 (xor_3_out, A[2], B[2]);
  xor xor_4 (xor_4_out, A[3], B[3]);
  xor xor_5 (xor_5_out, A[4], B[4]);
  xor xor_6 (xor_6_out, A[5], B[5]);
  xor xor_7 (xor_7_out, A[6], B[6]);
  xor xor_8 (xor_8_out, A[7], B[7]);
  xor xor_9 (SUM0, xor_1_out, 1'b0);
  and and_2 (and_2_out, 1'b0, xor_1_out);
  and and_3 (and_3_out, A[0], B[0]);
  xor xor_10 (SUM1, xor_2_out, or_2_out);
  and and_4 (and_4_out, or_2_out, xor_2_out);
  and and_5 (and_5_out, A[1], B[1]);
  xor xor_11 (SUM2, xor_3_out, or_3_out);
  and and_6 (and_6_out, or_3_out, xor_3_out);
  and and_7 (and_7_out, A[2], B[2]);
  xor xor_12 (SUM3, xor_4_out, or_4_out);
  and and_8 (and_8_out, or_4_out, xor_4_out);
  and and_9 (and_9_out, A[3], B[3]);
  xor xor_13 (SUM4, xor_5_out, or_5_out);
  and and_10 (and_10_out, or_5_out, xor_5_out);
  and and_11 (and_11_out, A[4], B[4]);
  xor xor_14 (SUM5, xor_6_out, or_6_out);
  and and_12 (and_12_out, or_6_out, xor_6_out);
  and and_13 (and_13_out, A[5], B[5]);
  xor xor_15 (SUM6, xor_7_out, or_7_out);
  and and_14 (and_14_out, or_7_out, xor_7_out);
  and and_15 (and_15_out, A[6], B[6]);
  xor xor_16 (SUM7, xor_8_out, or_8_out);
  and and_16 (and_16_out, or_8_out, xor_8_out);
  and and_17 (and_17_out, A[7], B[7]);
  assign CompOR = A | B;  // OR_Gate or_1, 8 bits wide
  or or_2 (or_2_out, and_2_out, and_3_out);
  or or_3 (or_3_out, and_4_out, and_5_out);
  or or_4 (or_4_out, and_6_out, and_7_out);
  or or_5 (or_5_out, and_8_out, and_9_out);
  or or_6 (or_6_out, and_10_out, and_11_out);
  or or_7 (or_7_out, and_12_out, and_13_out);
  or or_8 (or_8_out, and_14_out, and_15_out);
  or or_9 (CoutSuma, and_16_out, and_17_out);
  assign CompNAND = ~(A & B);  // NAND_Gate nand_1, 8 bits wide
  not not_1 (not_1_out, B[0]);
  not not_2 (not_2_out, B[1]);
  not not_3 (not_3_out, B[2]);
  not not_4 (not_4_out, B[3]);
  not not_5 (not_5_out, B[4]);
  not not_6 (not_6_out, B[5]);
  not not_7 (not_7_out, B[6]);
  not not_8 (not_8_out, B[7]);
  xor xor_17 (xor_17_out, A[0], not_1_out);
  xor xor_18 (xor_18_out, A[1], not_2_out);
  xor xor_19 (xor_19_out, A[2], not_3_out);
  xor xor_20 (xor_20_out, A[3], not_4_out);
  xor xor_21 (xor_21_out, A[4], not_5_out);
  xor xor_22 (xor_22_out, A[5], not_6_out);
  xor xor_23 (xor_23_out, A[6], not_7_out);
  xor xor_24 (xor_24_out, A[7], not_8_out);
  assign CompXOR = A ^ B;  // XOR_Gate xor_25, 8 bits wide
  xor xor_26 (RES0, xor_17_out, 1'b1);
  and and_18 (and_18_out, 1'b1, xor_17_out);
  and and_19 (and_19_out, A[0], not_1_out);
  xor xor_27 (RES1, xor_18_out, or_10_out);
  and and_20 (and_20_out, or_10_out, xor_18_out);
  and and_21 (and_21_out, A[1], not_2_out);
  xor xor_28 (RES2, xor_19_out, or_11_out);
  and and_22 (and_22_out, or_11_out, xor_19_out);
  and and_23 (and_23_out, A[2], not_3_out);
  xor xor_29 (RES3, xor_20_out, or_12_out);
  and and_24 (and_24_out, or_12_out, xor_20_out);
  and and_25 (and_25_out, A[3], not_4_out);
  xor xor_30 (RES4, xor_21_out, or_13_out);
  and and_26 (and_26_out, or_13_out, xor_21_out);
  and and_27 (and_27_out, A[4], not_5_out);
  xor xor_31 (RES5, xor_22_out, or_14_out);
  and and_28 (and_28_out, or_14_out, xor_22_out);
  and and_29 (and_29_out, A[5], not_6_out);
  xor xor_32 (RES6, xor_23_out, or_15_out);
  and and_30 (and_30_out, or_15_out, xor_23_out);
  and and_31 (and_31_out, A[6], not_7_out);
  xor xor_33 (RES7, xor_24_out, or_16_out);
  and and_32 (and_32_out, or_16_out, xor_24_out);
  and and_33 (and_33_out, A[7], not_8_out);
  or or_10 (or_10_out, and_18_out, and_19_out);
  or or_11 (or_11_out, and_20_out, and_21_out);
  or or_12 (or_12_out, and_22_out, and_23_out);
  or or_13 (or_13_out, and_24_out, and_25_out);
  or or_14 (or_14_out, and_26_out, and_27_out);
  or or_15 (or_15_out, and_28_out, and_29_out);
  or or_16 (or_16_out, and_30_out, and_31_out);
  or or_17 (or_17_out, and_32_out, and_33_out);
  not not_9 (CoutResta, or_17_out);
  ExactlyOne xor_34 (
    .out(Zero), .in0(Salida[0]), .in1(Salida[1]), .in2(Salida[2]), .in3(Salida[3]), .in4(1'b1),
    .in5(Salida[4]), .in6(Salida[5]), .in7(Salida[6]), .in8(Salida[7]));
  and and_34 (and_34_out, Selector[0], ~Selector[1], ~Selector[2], AND0);  // AND_Gate
  and and_35 (and_35_out, ~Selector[0], Selector[1], ~Selector[2], CompOR[0]);  // AND_Gate
  and and_36 (and_36_out, Selector[0], Selector[1], ~Selector[2], CompNAND[0]);  // AND_Gate
  and and_37 (and_37_out, ~Selector[0], ~Selector[1], Selector[2], CompXOR[0]);  // AND_Gate
  and and_38 (and_38_out, Selector[0], ~Selector[1], Selector[2], SUM0);  // AND_Gate
  and and_39 (and_39_out, ~Selector[0], Selector[1], Selector[2], RES0);  // AND_Gate
  and and_40 (and_40_out, Selector[0], ~Selector[1], ~Selector[2], AND1);  // AND_Gate
  and and_41 (and_41_out, ~Selector[0], Selector[1], ~Selector[2], CompOR[1]);  // AND_Gate
  and and_42 (and_42_out, Selector[0], Selector[1], ~Selector[2], CompNAND[1]);  // AND_Gate
  and and_43 (and_43_out, ~Selector[0], ~Selector[1], Selector[2], CompXOR[1]);  // AND_Gate
  and and_44 (and_44_out, Selector[0], ~Selector[1], Selector[2], SUM1);  // AND_Gate
  and and_45 (and_45_out, ~Selector[0], Selector[1], Selector[2], RES1);  // AND_Gate
  and and_46 (and_46_out, Selector[0], ~Selector[1], ~Selector[2], AND2);  // AND_Gate
  and and_47 (and_47_out, ~Selector[0], Selector[1], ~Selector[2], CompOR[2]);  // AND_Gate
  and and_48 (and_48_out, Selector[0], Selector[1], ~Selector[2], CompNAND[2]);  // AND_Gate
  and and_49 (and_49_out, ~Selector[0], ~Selector[1], Selector[2], CompXOR[2]);  // AND_Gate
  and and_50 (and_50_out, Selector[0], ~Selector[1], Selector[2], SUM2);  // AND_Gate
  and and_51 (and_51_out, ~Selector[0], Selector[1], Selector[2], RES2);  // AND_Gate
  and and_52 (and_52_out, Selector[0], ~Selector[1], ~Selector[2], AND3);  // AND_Gate
  and and_53 (and_53_out, ~Selector[0], Selector[1], ~Selector[2], CompOR[3]);  // AND_Gate
  and and_54 (and_54_out, Selector[0], Selector[1], ~Selector[2], CompNAND[3]);  // AND_Gate
  and and_55 (and_55_out, ~Selector[0], ~Selector[1], Selector[2], CompXOR[3]);  // AND_Gate
  and and_56 (and_56_out, Selector[0], ~Selector[1], Selector[2], SUM3);  // AND_Gate
  and and_57 (and_57_out, ~Selector[0], Selector[1], Selector[2], RES3);  // AND_Gate
  and and_58 (and_58_out, Selector[0], ~Selector[1], ~Selector[2], AND4);  // AND_Gate
  and and_59 (and_59_out, ~Selector[0], Selector[1], ~Selector[2], CompOR[4]);  // AND_Gate
  and and_60 (and_60_out, Selector[0], Selector[1], ~Selector[2], CompNAND[4]);  // AND_Gate
  and and_61 (and_61_out, ~Selector[0], ~Selector[1], Selector[2], CompXOR[4]);  // AND_Gate
  and and_62 (and_62_out, Selector[0], ~Selector[1], Selector[2], SUM4);  // AND_Gate
  and and_63 (and_63_out, ~Selector[0], Selector[1], Selector[2], RES4);  // AND_Gate
  and and_64 (and_64_out, Selector[0], ~Selector[1], ~Selector[2], AND5);  // AND_Gate
  and and_65 (and_65_out, ~Selector[0], Selector[1], ~Selector[2], CompOR[5]);  // AND_Gate
  and and_66 (and_66_out, Selector[0], Selector[1], ~Selector[2], CompNAND[5]);  // AND_Gate
  and and_67 (and_67_out, ~Selector[0], ~Selector[1], Selector[2], CompXOR[5]);  // AND_Gate
  and and_68 (and_68_out, Selector[0], ~Selector[1], Selector[2], SUM5);  // AND_Gate
  and and_69 (and_69_out, ~Selector[0], Selector[1], Selector[2], RES5);  // AND_Gate
  and and_70 (and_70_out, Selector[0], ~Selector[1], ~Selector[2], AND6);  // AND_Gate
  and and_71 (and_71_out, ~Selector[0], Selector[1], ~Selector[2], CompOR[6]);  // AND_Gate
  and and_72 (and_72_out, Selector[0], Selector[1], ~Selector[2], CompNAND[6]);  // AND_Gate
  and and_73 (and_73_out, ~Selector[0], ~Selector[1], Selector[2], CompXOR[6]);  // AND_Gate
  and and_74 (and_74_out, Selector[0], ~Selector[1], Selector[2], SUM6);  // AND_Gate
  and and_75 (and_75_out, ~Selector[0], Selector[1], Selector[2], RES6);  // AND_Gate
  and and_76 (and_76_out, Selector[0], ~Selector[1], ~Selector[2], AND7);  // AND_Gate
  and and_77 (and_77_out, ~Selector[0], Selector[1], ~Selector[2], CompOR[7]);  // AND_Gate
  and and_78 (and_78_out, Selector[0], Selector[1], ~Selector[2], CompNAND[7]);  // AND_Gate
  and and_79 (and_79_out, ~Selector[0], ~Selector[1], Selector[2], CompXOR[7]);  // AND_Gate
  and and_80 (and_80_out, Selector[0], ~Selector[1], Selector[2], SUM7);  // AND_Gate
  and and_81 (and_81_out, ~Selector[0], Selector[1], Selector[2], RES7);  // AND_Gate
  and and_82 (and_82_out, Selector[0], ~Selector[1], Selector[2], CoutSuma);  // AND_Gate
  and and_83 (and_83_out, ~Selector[0], Selector[1], Selector[2], CoutResta);  // AND_Gate
  or or_18 (Salida[0], and_34_out, and_35_out, and_36_out, and_37_out, and_38_out, and_39_out);
  or or_19 (Salida[1], and_40_out, and_41_out, and_42_out, and_43_out, and_44_out, and_45_out);
  or or_20 (Salida[2], and_46_out, and_47_out, and_48_out, and_49_out, and_50_out, and_51_out);
  or or_21 (Salida[3], and_52_out, and_53_out, and_54_out, and_55_out, and_56_out, and_57_out);
  or or_22 (Salida[4], and_58_out, and_59_out, and_60_out, and_61_out, and_62_out, and_63_out);
  or or_23 (Salida[5], and_64_out, and_65_out, and_66_out, and_67_out, and_68_out, and_69_out);
  or or_24 (Salida[6], and_70_out, and_71_out, and_72_out, and_73_out, and_74_out, and_75_out);
  or or_25 (Salida[7], and_76_out, and_77_out, and_78_out, and_79_out, and_80_out, and_81_out);
  or or_26 (Cout, and_82_out, and_83_out);

  // Other names for the same wires on the sheet: CompAND[7:0] = {AND7, AND6, AND5, AND4, AND3, AND2, AND1, AND0};
  //   NAND0 = CompNAND[0]; NAND1 = CompNAND[1]; NAND2 = CompNAND[2]; NAND3 = CompNAND[3]; NAND4 = CompNAND[4];
  //   NAND5 = CompNAND[5]; NAND6 = CompNAND[6]; NAND7 = CompNAND[7]; OR0 = CompOR[0]; OR1 = CompOR[1];
  //   OR2 = CompOR[2]; OR3 = CompOR[3]; OR4 = CompOR[4]; OR5 = CompOR[5]; OR6 = CompOR[6]; OR7 = CompOR[7];
  //   XOR0 = CompXOR[0]; XOR1 = CompXOR[1]; XOR2 = CompXOR[2]; XOR3 = CompXOR[3]; XOR4 = CompXOR[4];
  //   XOR5 = CompXOR[5]; XOR6 = CompXOR[6]; XOR7 = CompXOR[7];
  //   Restador[7:0] = {RES7, RES6, RES5, RES4, RES3, RES2, RES1, RES0}; S[7:0] = Salida; S0 = Salida[0];
  //   S1 = Salida[1]; S2 = Salida[2]; S3 = Salida[3]; S4 = Salida[4]; S5 = Salida[5]; S6 = Salida[6]; S7 = Salida[7];
  //   Sumador[7:0] = {SUM7, SUM6, SUM5, SUM4, SUM3, SUM2, SUM1, SUM0}
endmodule
